# Fritzing sketch diagram (saved by Fritzing 1.0.3b)
breadboards: 1

parts:
  Mod1 = Raspberry Pi 4B
  RHT1 = Humidity and Temperature Sensor RHT03
  HC-SR04_Sensor_1 = HC-SR04 Ultrasonic Distance Sensor
  R1 = Resistor [tolerance=±5% power=0.25W resistance=1000 package=THT]
  R2 = Resistor [tolerance=±5% power=0.25W resistance=2000 package=THT]
  LED1 = RGB LED - (4 legs) [color="Red (633nm)" current=0.030A package="5 mm [THT]"]
  R3 = Resistor [tolerance=±5% power=0.25W resistance=220 package=THT]
  R4 = Resistor [tolerance=±5% power=0.25W resistance=220 package=THT]
  R5 = Resistor [tolerance=±5% power=0.25W resistance=220 package=THT]
  J1 = Piezo Speaker
  Q1 = NPN-Transistor [package="TO92 [THT]"]

nets:
  N1: Mod1.3V3, LED1.common_anode
  VCC: Mod1.5V, RHT1.Vcc, HC-SR04_Sensor_1.VCC
  GND: Mod1.GND, RHT1.GND_2, HC-SR04_Sensor_1.GND, R2.Pin_0, J1.pin1, Q1.E
  N2: Mod1.GPIO27, Q1.B
  N3: Mod1.GPIO6, RHT1.GND_1
  N4: Mod1.GPIO13, R3.Pin_0
  N5: Mod1.GPIO19, R4.Pin_0
  N6: Mod1.GPIO16, R1.Pin_0, R2.Pin_1
  N7: Mod1.GPIO26, R5.Pin_0
  N8: HC-SR04_Sensor_1.ECHO, R1.Pin_1
  N9: LED1.red_cathode, R3.Pin_1
  N10: LED1.green_cathode, R4.Pin_1
  N11: LED1.blue_cathode, R5.Pin_1
  N12: J1.pin2, Q1.C
